# Fritzing sketch APDS9301 (saved by Fritzing 0.8.5b)
breadboards: 1

parts:
  APDS9301 = IC, DIP package, 6 pins [chip_label=IC1]
  Parte1 = Arduino Mega 2560 (Rev3)

nets:
  N1: APDS9301.pin1, Parte1.3V3
  N2: APDS9301.pin2, APDS9301.pin3, Parte1.GND
  N3: APDS9301.pin4, Parte1.D2_PWM
  N4: APDS9301.pin5, Parte1.SDA
  N5: APDS9301.pin6, Parte1.SCL
